# Fritzing sketch DSI (saved by Fritzing 0.9.3b)
circuit board: 30.7405cm x 20.0281cm
breadboards: 1

parts:
  Q2 = NPN-Transistor [package="TO92 [THT]"]
  R1 = Resistor [tolerance=±5% resistance=10k package=THT]
  Part1 = Arduino Uno (Rev3)
  LCD1 = LCD screen
  LCM1602_IIC2 = LCM1602 IIC [part_number="LCM1602 IIC" chip_label="LCM1602 IIC" package="DIP (Dual Inline) [THT]"]
  U1 = MAX6675 [package=so08]
  Q1 = Basic FET N-Channel [package="D2Pak [SMD]"]
  R2 = Heating Pad
  VCC1 = Battery block 9V
  R3 = Temperature Sensor (Thermistor) [thermistor_type=NTC package=THT]

nets:
  N1: Q2.E, Q1.source
  N2: Q2.C, R1.Pin_0, Q1.Gate, R2.pin_1
  N3: R1.Pin_1, VCC1.+
  N4: Part1.A4/SDA, LCM1602_IIC2.SDA
  N5: Part1.A5/SCL, LCM1602_IIC2.SCL
  N6: Part1.D8, U1.MISO
  N7: Part1.D9_PWM, U1.CS
  N8: Part1.D10_PWM/SS, U1.SCK
  GND: Part1.GND, LCM1602_IIC2.GND, U1.VSS
  5V: Part1.5V, LCM1602_IIC2.VCC, U1.VDD
  VSS: LCD1.VSS, LCM1602_IIC2.VSS
  VDD: LCD1.VDD, LCM1602_IIC2.VDD
  N9: LCD1.V0, LCM1602_IIC2.V0
  N10: LCD1.RS, LCM1602_IIC2.RS
  N11: LCD1.R/W, LCM1602_IIC2.RW
  N12: LCD1.E, LCM1602_IIC2.E
  N13: LCD1.DB0, LCM1602_IIC2.D0
  N14: LCD1.DB1, LCM1602_IIC2.D1
  N15: LCD1.DB2, LCM1602_IIC2.D2
  N16: LCD1.DB3, LCM1602_IIC2.D3
  N17: LCD1.DB4, LCM1602_IIC2.D4
  N18: LCD1.DB5, LCM1602_IIC2.D5
  N19: LCD1.DB6, LCM1602_IIC2.D6
  N20: LCD1.DB7, LCM1602_IIC2.D7
  N21: LCD1.LED+, LCM1602_IIC2.A
  N22: LCD1.LED-, LCM1602_IIC2.K
  N23: LCM1602_IIC2.LED_A, LCM1602_IIC2.LED_B
  N24: U1.T-, R3.pin_1
  N25: U1.T+, R3.pin_0
  N26: R2.pin_0, VCC1.-

custom parts:
  LCM1602 IIC: I2C-Module to use a 1602 or 2004 LCD on with the wire.h libory Serial LCD Modul
  Heating Pad: A thermoresistant material with an embeded conductor that dissipates electrical energy into heat.
