# Fritzing sketch Untitled Sketch1 (saved by Fritzing 0.9.3b)
breadboards: 1

parts:
  Part3 = Arduino Uno (Rev3) - ICSP
  U5 = MAX6675 [package=so08]
  Part4 = LCD1602-I2C
  R4 = Heating Pad
  R5 = Temperature Sensor (Thermistor) [thermistor_type=NTC package=THT]
  Q3 = TRANSISTOR_NPN [package=to-92-ammo]
  Q4 = Basic FET N-Channel [package="TO220 [THT]"]
  R6 = Resistor [tolerance=±5% resistance=10k package=THT]
  U6 = LIPO-1000mAh [package=lipo-1000]
  ENCODER1 = Rotary Encoder with Knob
  R7 = Resistor [tolerance=±5% resistance=10k package=THT]
  R8 = Resistor [tolerance=±5% resistance=10k package=THT]
  R9 = Resistor [tolerance=±5% resistance=10k package=THT]

nets:
  N1: Part3.A4/SDA, Part4.SDA
  N2: Part3.A5/SCL, Part4.SCL
  5V: Part3.5V, U5.VDD, Part4.VCC
  N3: Part3.D9_PWM, Q3.B
  N4: Part3.D12/MISO, ENCODER1.no_name_yet#3, R8.Pin_0
  N5: Part3.D13/SCK, ENCODER1.no_name_yet#1, R7.Pin_0
  N6: Part3.D3_PWM, U5.SCK
  N7: Part3.D4, U5.CS
  N8: Part3.D5_PWM, U5.MISO
  N9: Part3.D7, R4.pin_0, R6.Pin_1, U6.+, R7.Pin_1, R8.Pin_1, R9.Pin_0
  GND: Part3.GND, U5.VSS, Part4.GND, Q3.E, Q4.source, U6.-, ENCODER1.no_name_yet#2, ENCODER1.no_name_yet#4
  N10: U5.T-, R5.pin_1
  N11: U5.T+, R5.pin_0
  N12: R4.pin_1, Q4.drain
  N13: Q3.C, Q4.gate, R6.Pin_0
  N14: ENCODER1.no_name_yet#5, R9.Pin_1

custom parts:
  LCD1602-I2C: A standard character display, usually with 2x16 characters. Comes in many colors with LCM1602 IIC attached.
  Heating Pad: A thermoresistant material with an embeded conductor that dissipates electrical energy into heat.
  Rotary Encoder with Knob: Rotary Encoder with 1/4" Shaft and Knob
